# Fritzing sketch tensao_baseado_lm675 (saved by Fritzing 0.9.3b)
circuit board: 5cm x 5cm
breadboards: 1

parts:
  GND_V = Screw terminal - 2 pins [package=THT]
  -v-gnd-+v = female pin header, 3 pins [form="♀ (female)"]
  R1 = Resistor [tolerance=±5% resistance=22k package=THT]
  R2 = Resistor [tolerance=±5% resistance=22k package=THT]
  R3 = Resistor [tolerance=±5% resistance=1k package=THT]
  R4 = Resistor [tolerance=±5% resistance=15k package=THT]
  lm675 = female pin header, 5 pins [form="♀ (female)"]
  lm676 = female pin header, 5 pins [form="♀ (female)"]

nets:
  GND: GND_V.pin1, -v-gnd-+v.pin3, R2.Pin_1, lm675.pin3, lm676.pin3
  N1: GND_V.pin2, -v-gnd-+v.pin1, R1.Pin_0, lm675.pin5, lm676.pin5
  N2: -v-gnd-+v.pin2, R4.Pin_1, lm675.pin4, lm676.pin4
  N3: R1.Pin_1, R2.Pin_0, R3.Pin_0, lm675.pin1, lm676.pin1
  N4: R3.Pin_1, R4.Pin_0, lm675.pin2, lm676.pin2
