# Fritzing sketch gerador_ad9833_versao_2 (saved by Fritzing 0.9.3b)
circuit board: 10cm x 10cm
breadboards: 1

parts:
  arduino_nano = Arduino Nano (Rev3.0)
  GND_5V = female pin header, 2 pins [form="♀ (female)"]
  1=Vcc_2=DGND_3=SDATA_4=SCLK_5=FSYNC_6=AGND_7=OUT = female pin header, 7 pins [form="♀ (female)"]
  1=AGND_2=OUT_MOD = female pin header, 2 pins [form="♀ (female)"]
  C1 = Ceramic Capacitor [capacitance=100nF package="100 mil [THT, multilayer]"]
  R1 = Resistor [tolerance=±5% resistance=680k package=THT]
  1=GND_2=IN_PA = female pin header, 2 pins [form="♀ (female)"]
  1=GND_2_=OUT_PA = female pin header, 2 pins [form="♀ (female)"]
  1=GND_2_=IN_SEG = female pin header, 2 pins [form="♀ (female)"]
  TL72_SEGUIDOR = LM741 [part_number=LM741 package="DIP (Dual Inline) [THT]"]
  1=GND_2=OUT_SEG = female pin header, 2 pins [form="♀ (female)"]
  1=GND_2=IN_GAIN = female pin header, 2 pins [form="♀ (female)"]
  TL72_GANHO/SEG = LM741 [part_number=LM741 package="DIP (Dual Inline) [THT]"]
  trimpot = TRIMPOT [package=3386u]
  R3 = Resistor [tolerance=±5% resistance=1k package=THT]
  1=GND_2_=saidaGanho = female pin header, 2 pins [form="♀ (female)"]
  1=I2C_CLK_2=I2C_DATA_3=SPI_SCK_4=SPI_MISO_5=SPI_MOSI_6=SPI_SS_7=UART_IN_8=UART_OUT = female pin header, 8 pins [form="♀ (female)"]
  1=gnd_2=3_3v_3=5v = female pin header, 3 pins [form="♀ (female)"]
  1=gnd_2=saida_modulo_3=saida_filtro_PA_4=saida_seguidor_5=saida_seguidor-alternativo_6=saida_ganho = female pin header, 6 pins [form="♀ (female)"]
  1=GND_2=OUT_SEG_ALT = female pin header, 2 pins [form="♀ (female)"]
  1=GND_2=IN_SEG_ALT = female pin header, 2 pins [form="♀ (female)"]

nets:
  N1: arduino_nano.D1/TX, 1=I2C_CLK_2=I2C_DATA_3=SPI_SCK_4=SPI_MISO_5=SPI_MOSI_6=SPI_SS_7=UART_IN_8=UART_OUT.pin8
  N2: arduino_nano.D0/RX, 1=I2C_CLK_2=I2C_DATA_3=SPI_SCK_4=SPI_MISO_5=SPI_MOSI_6=SPI_SS_7=UART_IN_8=UART_OUT.pin7
  GND: arduino_nano.GND, GND_5V.pin1, 1=Vcc_2=DGND_3=SDATA_4=SCLK_5=FSYNC_6=AGND_7=OUT.pin2, 1=Vcc_2=DGND_3=SDATA_4=SCLK_5=FSYNC_6=AGND_7=OUT.pin6, 1=AGND_2=OUT_MOD.pin1, 1=gnd_2=3_3v_3=5v.pin1, 1=gnd_2=saida_modulo_3=saida_filtro_PA_4=saida_seguidor_5=saida_seguidor-alternativo_6=saida_ganho.pin1, 1=GND_2=OUT_SEG_ALT.pin1
  N3: arduino_nano.D9, 1=Vcc_2=DGND_3=SDATA_4=SCLK_5=FSYNC_6=AGND_7=OUT.pin5
  N4: arduino_nano.D10, 1=I2C_CLK_2=I2C_DATA_3=SPI_SCK_4=SPI_MISO_5=SPI_MOSI_6=SPI_SS_7=UART_IN_8=UART_OUT.pin6
  N5: arduino_nano.D11/MOSI, 1=Vcc_2=DGND_3=SDATA_4=SCLK_5=FSYNC_6=AGND_7=OUT.pin3, 1=I2C_CLK_2=I2C_DATA_3=SPI_SCK_4=SPI_MISO_5=SPI_MOSI_6=SPI_SS_7=UART_IN_8=UART_OUT.pin5
  N6: arduino_nano.D12/MISO, 1=I2C_CLK_2=I2C_DATA_3=SPI_SCK_4=SPI_MISO_5=SPI_MOSI_6=SPI_SS_7=UART_IN_8=UART_OUT.pin4
  N7: arduino_nano.5V, GND_5V.pin2, 1=Vcc_2=DGND_3=SDATA_4=SCLK_5=FSYNC_6=AGND_7=OUT.pin1, 1=gnd_2=3_3v_3=5v.pin3
  N8: arduino_nano.A5, 1=I2C_CLK_2=I2C_DATA_3=SPI_SCK_4=SPI_MISO_5=SPI_MOSI_6=SPI_SS_7=UART_IN_8=UART_OUT.pin1
  N9: arduino_nano.A4, 1=I2C_CLK_2=I2C_DATA_3=SPI_SCK_4=SPI_MISO_5=SPI_MOSI_6=SPI_SS_7=UART_IN_8=UART_OUT.pin2
  N10: arduino_nano.3V3, 1=gnd_2=3_3v_3=5v.pin2
  N11: arduino_nano.D13/SCK, 1=Vcc_2=DGND_3=SDATA_4=SCLK_5=FSYNC_6=AGND_7=OUT.pin4, 1=I2C_CLK_2=I2C_DATA_3=SPI_SCK_4=SPI_MISO_5=SPI_MOSI_6=SPI_SS_7=UART_IN_8=UART_OUT.pin3
  N12: 1=Vcc_2=DGND_3=SDATA_4=SCLK_5=FSYNC_6=AGND_7=OUT.pin7, 1=AGND_2=OUT_MOD.pin2, 1=gnd_2=saida_modulo_3=saida_filtro_PA_4=saida_seguidor_5=saida_seguidor-alternativo_6=saida_ganho.pin2
  N13: C1.0, R1.Pin_0, 1=GND_2_=OUT_PA.pin2, 1=gnd_2=saida_modulo_3=saida_filtro_PA_4=saida_seguidor_5=saida_seguidor-alternativo_6=saida_ganho.pin3
  N14: C1.1, 1=GND_2=IN_PA.pin2
  N15: R1.Pin_1, 1=GND_2=IN_PA.pin1, 1=GND_2_=OUT_PA.pin1
  N16: 1=GND_2_=IN_SEG.pin1, 1=GND_2=OUT_SEG.pin1
  N17: 1=GND_2_=IN_SEG.pin2, TL72_SEGUIDOR.pin3
  N18: TL72_SEGUIDOR.pin1, TL72_SEGUIDOR.pin2, 1=GND_2=OUT_SEG.pin2, 1=gnd_2=saida_modulo_3=saida_filtro_PA_4=saida_seguidor_5=saida_seguidor-alternativo_6=saida_ganho.pin4
  N19: 1=GND_2=IN_GAIN.pin1, R3.Pin_1, 1=GND_2_=saidaGanho.pin1
  N20: 1=GND_2=IN_GAIN.pin2, TL72_GANHO/SEG.pin3
  N21: TL72_GANHO/SEG.pin1, trimpot.CW, 1=GND_2_=saidaGanho.pin2, 1=gnd_2=saida_modulo_3=saida_filtro_PA_4=saida_seguidor_5=saida_seguidor-alternativo_6=saida_ganho.pin6
  N22: TL72_GANHO/SEG.pin2, trimpot.CCW, trimpot.WIPER, R3.Pin_0
  N23: TL72_GANHO/SEG.pin5, 1=GND_2=IN_SEG_ALT.pin2
  N24: TL72_GANHO/SEG.pin6, TL72_GANHO/SEG.pin7, 1=gnd_2=saida_modulo_3=saida_filtro_PA_4=saida_seguidor_5=saida_seguidor-alternativo_6=saida_ganho.pin5, 1=GND_2=OUT_SEG_ALT.pin2

custom parts:
  LM741: This is a single Op Amp DIP.
